// Logisim project Circuito CPU.circ as structural Verilog: 6 circuits, main circuit main
module main (
  input  [3:0] A,
  input  [3:0] B,
  output out_3,
  output [3:0] S,
  output [3:0] S_2,
  output [3:0] S_3,
  output [3:0] S_4
);

  wire or_4_1_p1;

  add_4 add_4_1 (.S(S_2), .Overflow(out_3), .A(A), .B(A));
  // OR_4 or_4_1: pin names not known; wires that end beside it: or_4_1_p1, or_4_1_p1
  Not_4 not_4_1 ();  // open: B, S

  assign S = B;
endmodule

module Add_1 (
  input  A,
  input  B,
  input  Vem_1,
  output S,
  output Vai_1
);

  wire and_1_out, and_2_out, and_3_out, and_4_out, and_5_out, and_6_out, and_7_out, not_1_out, not_2_out,
       not_3_out, not_4_out, not_5_out, not_6_out;

  not not_1 (not_1_out, A);
  not not_2 (not_2_out, B);
  not not_3 (not_3_out, A);
  not not_4 (not_4_out, Vem_1);
  not not_5 (not_5_out, B);
  not not_6 (not_6_out, Vem_1);
  and and_1 (and_1_out, B, Vem_1);
  and and_2 (and_2_out, A, Vem_1);
  and and_3 (and_3_out, A, B);
  and and_4 (and_4_out, not_1_out, not_2_out, Vem_1);
  and and_5 (and_5_out, not_3_out, B, not_4_out);
  and and_6 (and_6_out, A, not_5_out, not_6_out);
  and and_7 (and_7_out, A, B, Vem_1);
  or or_1 (Vai_1, and_1_out, and_2_out, and_3_out);
  or or_2 (S, and_4_out, and_5_out, and_6_out, and_7_out);
endmodule

module add_4 (
  input  [3:0] A,
  input  [3:0] B,
  output Overflow,
  output [3:0] S
);

  wire add_1_2_vai_1, add_1_3_vai_1, add_1_4_vai_1;

  // Probe on A
  Add_1 add_1_1 (.A(A[3]), .B(B[3]), .Vem_1(add_1_2_vai_1), .S(S[3]), .Vai_1(Overflow));
  Add_1 add_1_2 (.A(A[2]), .B(B[2]), .Vem_1(add_1_3_vai_1), .S(S[2]), .Vai_1(add_1_2_vai_1));
  Add_1 add_1_3 (.A(A[1]), .B(B[1]), .Vem_1(add_1_4_vai_1), .S(S[1]), .Vai_1(add_1_3_vai_1));
  // Probe on S
  Add_1 add_1_4 (.A(A[0]), .B(B[0]), .Vem_1(1'b0), .S(S[0]), .Vai_1(add_1_4_vai_1));
  // Probe on B
endmodule

module OR_4 (
  input  [3:0] B,
  input  [3:0] A,
  output [3:0] S
);

  or or_1 (S[3], A[3], B[3]);
  or or_2 (S[1], A[1], B[1]);
  or or_3 (S[2], A[2], B[2]);
  or or_4 (S[0], A[0], B[0]);
endmodule

module Not_4 (
  input  [3:0] B,
  output [3:0] S
);

  not not_1 (S[3], B[3]);
  not not_2 (S[2], B[2]);
  not not_3 (S[1], B[1]);
  not not_4 (S[0], B[0]);
endmodule

module Buffer (
  input  [3:0] B,
  input  in_2,
  output [3:0] out_3
);

  assign out_3[2] = in_2 ? B[2] : 1'bz;  // Controlled_Buffer controlled_buffer_1
  assign out_3[3] = in_2 ? B[3] : 1'bz;  // Controlled_Buffer controlled_buffer_2
  assign out_3[1] = in_2 ? B[1] : 1'bz;  // Controlled_Buffer controlled_buffer_3
  assign out_3[0] = in_2 ? B[0] : 1'bz;  // Controlled_Buffer controlled_buffer_4
endmodule
